# Fritzing sketch pomodoro-timer (saved by Fritzing 0.9.3b)

parts:
  S1 = Pushbutton [package="[THT]"]
  VCC1 = 4 x AAA Battery Mount
  S2 = Toggle Switch [package=THT]
  Adafruit_Atmega32u1 = Adafruit Atmega32u4 Breakout Board [part_number="Atmega 32u4"]

nets:
  N1: S1.Pin_1, S1.Pin_2, Adafruit_Atmega32u1.RST
  N2: S1.Pin_3, S1.Pin_4, Adafruit_Atmega32u1.GND#36
  N3: VCC1.-, S2.L2
  N4: VCC1.+, Adafruit_Atmega32u1.VCC
  N5: S2.COM, Adafruit_Atmega32u1.GND#14
